# Fritzing sketch NE555_astabil (saved by Fritzing 0.9.3b)
circuit board: 4cm x 3.5cm
breadboards: 1

parts:
  IC1 = General purpose bipolar Timer [package=dil-08]
  D1 = Rectifier Diode [part_number=1N4001 package="300 mil [THT]"]
  LED1 = LED - 5mm [color="Red (633nm)" package="5 mm [THT]"]
  R4 = Resistor [tolerance=±5% resistance=470 package=THT]
  C2 = Ceramic Capacitor [capacitance=10nF package="200 mil [THT, multilayer]"]
  R1 = TRIMPOT [package=trim_pot_pth]
  R2 = TRIMPOT [package=trim_pot_pth]
  C3 = Tantalum Capacitor [capacitance=4.7µF package="200 mil [THT, tantalum]"]
  R4_2 = Resistor [tolerance=±5% resistance=1k package=THT]
  J1 = female pin header, 4 pins [form="♀ (female)"]

nets:
  N1: IC1.GND, LED1.cathode, C2.0, C3.+, J1.pin2, J1.pin4
  N2: IC1.TRI, IC1.TRE, D1.cathode, R2.WIPER, C3.-
  N3: IC1.OUT, R4.Pin_1, J1.pin3
  N4: IC1._RES, IC1.VCC+, R4_2.Pin_1, J1.pin1
  N5: IC1.CON, C2.1
  N6: IC1.DIS, D1.anode, R1.WIPER, R2.CCW
  N7: LED1.anode, R4.Pin_0
  N8: R1.CCW, R4_2.Pin_0

notes:
  NE555 Timer
  erfindergarden
  GND
  OUT
  VCC

custom parts:
  TRIMPOT: Various small potentiometers for set-and-forget applications
